# Fritzing sketch rc_perfboard2 (saved by Fritzing 0.9.3b)
perfboards: 4

parts:
  IC1 = L293D [package=THT]
  Part1 = Arduino Nano (Rev3.0)
  J1 = JST XH 2A male [form="♂ (male)" package=THT]
  J2 = JST XH 2A male [form="♂ (male)" package=THT]
  J3 = JST XH 2A male [form="♂ (male)" package=THT]
  J4 = JST XH 2A male [form="♂ (male)" package=THT]
  J5 = JST XH 2A male [form="♂ (male)" package=THT]
  IC2 = L293D [package=THT]
  Part2 = NRF24L01+ Breakout Board

nets:
  N1: IC1.Enable_1, Part1.D9
  N2: IC1.In_1, IC1.In_4, Part1.D3
  N3: IC1.Out_1_(_Controlled_by_Enable_1_), J2.pin2
  N4: IC1.0V, Part1.GND, J5.pin1, IC2.0V
  N5: IC1.Out_2_(_Controlled_by_Enable_1_), J2.pin1
  N6: IC1.In_2, IC1.In_3, Part1.D4
  N7: IC1.+Vmotor, Part1.VIN, J5.pin2, IC2.+Vmotor
  N8: IC1.Enable_2, Part1.D10
  N9: IC1.Out_3_(_Controlled_by_Enable_2_), J1.pin2
  N10: IC1.Out_4_(_Controlled_by_Enable_2_), J1.pin1
  N11: IC1.+V, Part1.5V, IC2.+V
  N12: Part1.D5, IC2.Enable_1
  N13: Part1.D6, IC2.Enable_2
  N14: Part1.D7, Part2.CE
  N15: Part1.D8, Part2.CS
  N16: Part1.D11/MOSI, Part2.MOSI
  N17: Part1.D12/MISO, Part2.MISO
  N18: Part1.A5, IC2.In_1, IC2.In_2
  N19: Part1.A0, IC2.In_3, IC2.In_4
  3V3: Part1.3V3, Part2.VCC
  N20: Part1.D13/SCK, Part2.SCK
  N21: J3.pin1, IC2.Out_3_(_Controlled_by_Enable_2_)
  N22: J3.pin2, IC2.Out_4_(_Controlled_by_Enable_2_)
  N23: J4.pin1, IC2.Out_2_(_Controlled_by_Enable_1_)
  N24: J4.pin2, IC2.Out_1_(_Controlled_by_Enable_1_)

notes:
  Motor 1
  Motor 2
  Motor 3
  Motor 4
  Ext_power

custom parts:
  JST XH 2A male: JST XH-2A
